# Fritzing sketch Untitled Sketch (saved by Fritzing 0.9.3b)
circuit board: 6.04505cm x 5.22753cm
breadboards: 1

parts:
  Led = Resistor [tolerance=±5% resistance=330 package=THT]
  Mitutoyo1 = Header 4 [package=1x04-1mm-ra]
  LED1 = LED - 5mm [color="Red (633nm)" package="5 mm [THT]"]
  LVDT2 = Rotary Potentiometer (Small) [maximum_resistance=100kΩ package=THT]
  Q4 = NPN-Transistor [package="TO92 [THT]"]
  Q3 = NPN-Transistor [package="TO92 [THT]"]
  Mitutoyo2 = Header 4 [package=1x04-1mm-ra]
  R10k2 = Resistor [tolerance=±5% resistance=10k package=THT]
  ArduinoNano = Arduino Nano (Rev3.0)
  R10k1 = Resistor [tolerance=±5% resistance=10k package=THT]
  LVDT1 = Rotary Potentiometer (Small) [maximum_resistance=100kΩ package=THT]

nets:
  N1: Led.Pin_0, LED1.anode
  N2: Led.Pin_1, LVDT2.leg1, ArduinoNano.5V, LVDT1.leg1
  N3: Mitutoyo1.1, LED1.cathode, LVDT2.leg2, Q4.C, Q3.C, Mitutoyo2.1, ArduinoNano.GND, LVDT1.leg2
  N4: Mitutoyo1.2, ArduinoNano.D2
  N5: Mitutoyo1.3, ArduinoNano.D3
  N6: Mitutoyo1.4, Q3.E
  N7: LVDT2.wiper, ArduinoNano.A1
  N8: Q4.E, Mitutoyo2.4
  N9: Q4.B, R10k1.Pin_0
  N10: Q3.B, R10k2.Pin_0
  N11: Mitutoyo2.2, ArduinoNano.D4
  N12: Mitutoyo2.3, ArduinoNano.D9
  N13: R10k2.Pin_1, ArduinoNano.D5
  N14: ArduinoNano.D6, R10k1.Pin_1
  N15: ArduinoNano.A0, LVDT1.wiper
